# Fritzing sketch AstroController2_20231102_1 (saved by Fritzing 1.0.1rc)
circuit board: 11cm x 7.6cm
breadboards: 1

parts:
  PICO = Raspberry Pi Pico
  IC_74HCT254 = IC, DIP package, 20 pins [chip_label=74HCT245P]
  RHEATH1 = Resistor [tolerance=±5% power=0.25 resistance=220k package=THT]
  Q1 = Basic FET N-Channel [package="TO220 [THT]"]
  JHEAT1 = female pin header, 5 pins [form="♀ (female)"]
  V3 = DC Power [voltage=12V]
  J12V = Generic male header - 2 pins [form="♂ (male)" package=THT]
  Q2 = Basic FET N-Channel [package="TO220 [THT]"]
  RHEATH2 = Resistor [tolerance=±5% power=0.25 resistance=220k package=THT]
  JHEAT2 = female pin header, 5 pins [form="♀ (female)"]
  Q3 = Basic FET N-Channel [package="TO220 [THT]"]
  RHEATH3 = Resistor [tolerance=±5% power=0.25 resistance=220k package=THT]
  JHEAT3 = female pin header, 5 pins [form="♀ (female)"]
  FW_DRV1 = ULN2003A [package="DIP16 [THT]"]
  CFW = Ceramic Capacitor [capacitance=10nF voltage=35V package="100 mil [THT, multilayer]"]
  R_FW_HALL1 = Resistor [tolerance=±5% power=0.25 resistance=10k package=THT]
  JFW = female pin header, 8 pins [form="♀ (female)"]
  R_TEMP3 = Resistor [tolerance=±5% power=0.25 resistance=4.7k package=THT]
  R_TEMP1 = Resistor [tolerance=±5% power=0.25 resistance=4.7 package=THT]
  R_TEMP2 = Resistor [tolerance=±5% power=0.25 resistance=4.7 package=THT]
  RHEATL1 = Resistor [tolerance=±5% power=0.25 resistance=220 package=THT]
  RHEATL2 = Resistor [tolerance=±5% power=0.25 resistance=220 package=THT]
  RHEATL3 = Resistor [tolerance=±5% power=0.25 resistance=220 package=THT]
  JMETEO = female pin header, 4 pins [form="♀ (female)"]
  CFOC = Ceramic Capacitor [capacitance=10nF voltage=35V package="100 mil [THT, multilayer]"]
  JFOC = female pin header, 5 pins [form="♀ (female)"]
  FOC_DRV1 = ULN2003A [package="DIP16 [THT]"]
  C_DC12 = Electrolytic Capacitor [capacitance=4.7mF voltage=50V package="200 mil [THT, electrolytic]"]
  C_DC5 = Electrolytic Capacitor [capacitance=0.1mF voltage=35V package="100 mil [THT, electrolytic]"]

nets:
  GND/METEO_GND: PICO.pin_3, PICO.pin_8, PICO.pin_13, PICO.pin_18, PICO.pin_23, PICO.pin_28, PICO.pin_33, PICO.pin_38, IC_74HCT254.pin19, RHEATH1.Pin_1, Q1.source, JHEAT1.pin1, V3.V-, J12V.GND, Q2.source, RHEATH2.Pin_1, JHEAT2.pin1, Q3.source, RHEATH3.Pin_1, JHEAT3.pin1, FW_DRV1.0V, CFW.1, JFW.pin2, JMETEO.pin1, CFOC.1, FOC_DRV1.0V, C_DC12.-, C_DC5.-
  FOC4: PICO.pin_4, FOC_DRV1.In_4
  FOC3: PICO.pin_5, FOC_DRV1.In_3
  FOC2: PICO.pin_6, FOC_DRV1.In_2
  FOC1: PICO.pin_7, FOC_DRV1.In_1
  FWM4: PICO.pin_9, FW_DRV1.In_7
  FWM3: PICO.pin_10, FW_DRV1.In_6
  FWM2: PICO.pin_11, FW_DRV1.In_5
  FWM1: PICO.pin_12, FW_DRV1.In_4
  FW_HALL: PICO.pin_20, R_FW_HALL1.Pin_1, JFW.pin3
  METEO_SCK: PICO.pin_21, JMETEO.pin2
  METEO_SDI: PICO.pin_22, JMETEO.pin3
  Heat_pw_1: PICO.pin_24, IC_74HCT254.pin4
  Heat_pw_2: PICO.pin_25, IC_74HCT254.pin3
  Heat_pw_3: PICO.pin_26, IC_74HCT254.pin2
  Heat_temp_1: PICO.pin_27, JHEAT1.pin3, R_TEMP1.Pin_0
  Heat_temp_2: PICO.pin_29, JHEAT2.pin3, R_TEMP2.Pin_0
  Heat_temp_3: PICO.pin_31, JHEAT3.pin3, R_TEMP3.Pin_0
  3.3V/METEO_VCC: PICO.pin_37, JHEAT1.pin4, JHEAT2.pin4, JHEAT3.pin4, R_FW_HALL1.Pin_0, R_TEMP3.Pin_1, R_TEMP1.Pin_1, R_TEMP2.Pin_1, JMETEO.pin4
  5V: PICO.pin_40, IC_74HCT254.pin1, IC_74HCT254.pin20, JFW.pin1, C_DC5.+
  N1: IC_74HCT254.pin16, RHEATL1.Pin_0
  N2: IC_74HCT254.pin17, RHEATL2.Pin_0
  N3: IC_74HCT254.pin18, RHEATL3.Pin_0
  N4: RHEATH1.Pin_0, Q1.gate, RHEATL1.Pin_1
  N5: Q1.drain, JHEAT1.pin2
  12V: JHEAT1.pin5, V3.V+, J12V.VIN, JHEAT2.pin5, JHEAT3.pin5, FW_DRV1.COM_-_Common, CFW.0, JFW.pin4, CFOC.0, JFOC.pin1, FOC_DRV1.COM_-_Common, C_DC12.+
  N6: Q2.gate, RHEATH2.Pin_0, RHEATL2.Pin_1
  N7: Q2.drain, JHEAT2.pin2
  N8: Q3.gate, RHEATH3.Pin_0, RHEATL3.Pin_1
  N9: Q3.drain, JHEAT3.pin2
  N10: FW_DRV1.Out_7, JFW.pin8
  N11: FW_DRV1.Out_6, JFW.pin7
  N12: FW_DRV1.Out_5, JFW.pin6
  N13: FW_DRV1.Out_4, JFW.pin5
  N14: JFOC.pin2, FOC_DRV1.Out_1
  N15: JFOC.pin3, FOC_DRV1.Out_2
  N16: JFOC.pin4, FOC_DRV1.Out_3
  N17: JFOC.pin5, FOC_DRV1.Out_4

notes:
  METEO
  capteur météo
  Roue à filtre
  Heater1
  Heater2
  Heater3
  PICO
  Focuseur

custom parts:
  Raspberry Pi Pico: Raspberry Pi Pico. Based around the RP2040 microcontroller the Pico is a low cost microcontroller device bringing Raspberry Pi quality, cost, and easy of use to the microcontroller space. Jan 2021, Split part in to two versions: tht (this one) and SMD. This one will drill holes for a .1 in header in pcb to allow plugging in the module as well as providing pads to solder the module to the top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
  Generic male header - 2 pins: Generic male header
