# Fritzing sketch Filterwheel (saved by Fritzing 1.0.1rc)
circuit board: 8.47cm x 6.64cm
breadboards: 1

parts:
  PICO = Raspberry Pi Pico
  C1 = Ceramic Capacitor [capacitance=10nF voltage=35V package="100 mil [THT, multilayer]"]
  J1 = female pin header, 8 pins [form="♀ (female)"]
  R_FW_HALL = Resistor [tolerance=±5% power=0.25 resistance=10k package=THT]
  FW_DRV = ULN2003A [package="DIP16 [THT]"]
  V1 = DC Power [voltage=12V]
  12V = Generic male header - 2 pins [form="♂ (male)" package=THT]

nets:
  GND: PICO.pin_3, PICO.pin_8, PICO.pin_13, PICO.pin_18, PICO.pin_23, PICO.pin_28, PICO.pin_33, PICO.pin_38, C1.1, J1.pin2, FW_DRV.0V, V1.V-, 12V.GND
  FW_HALL: PICO.pin_20, J1.pin3, R_FW_HALL.Pin_1
  FWM4: PICO.pin_24, FW_DRV.In_4
  FWM3: PICO.pin_25, FW_DRV.In_3
  FWM2: PICO.pin_26, FW_DRV.In_2
  FWM1: PICO.pin_27, FW_DRV.In_1
  3.3V: PICO.pin_36, R_FW_HALL.Pin_0
  5V: PICO.pin_40, J1.pin1
  12V: C1.0, J1.pin4, FW_DRV.COM_-_Common, V1.V+, 12V.VIN
  N1: J1.pin5, FW_DRV.Out_1
  N2: J1.pin6, FW_DRV.Out_2
  N3: J1.pin7, FW_DRV.Out_3
  N4: J1.pin8, FW_DRV.Out_4

custom parts:
  Raspberry Pi Pico: Raspberry Pi Pico. Based around the RP2040 microcontroller the Pico is a low cost microcontroller device bringing Raspberry Pi quality, cost, and easy of use to the microcontroller space. Jan 2021, Split part in to two versions: tht (this one) and SMD. This one will drill holes for a .1 in header in pcb to allow plugging in the module as well as providing pads to solder the module to the top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
  Generic male header - 2 pins: Generic male header
