# Fritzing sketch Focuser (saved by Fritzing 1.0.1rc)
circuit board: 8.47cm x 6.64cm
breadboards: 1

parts:
  PICO = Raspberry Pi Pico
  C1 = Ceramic Capacitor [capacitance=10nF voltage=35V package="100 mil [THT, multilayer]"]
  FOC_DRV = ULN2003A [package="DIP16 [THT]"]
  V1 = DC Power [voltage=12V]
  12V = Generic male header - 2 pins [form="♂ (male)" package=THT]
  JFOC = female pin header, 5 pins [form="♀ (female)"]

nets:
  GND: PICO.pin_3, PICO.pin_8, PICO.pin_13, PICO.pin_18, PICO.pin_23, PICO.pin_28, PICO.pin_33, PICO.pin_38, C1.1, FOC_DRV.0V, V1.V-, 12V.GND
  FOC1: PICO.pin_9, FOC_DRV.In_1
  FOC2: PICO.pin_10, FOC_DRV.In_2
  FOC3: PICO.pin_11, FOC_DRV.In_3
  FOC4: PICO.pin_12, FOC_DRV.In_4
  3.3V: PICO.pin_36
  5V: PICO.pin_40
  12V: C1.0, FOC_DRV.COM_-_Common, V1.V+, 12V.VIN, JFOC.pin1
  N1: FOC_DRV.Out_4, JFOC.pin5
  N2: FOC_DRV.Out_3, JFOC.pin4
  N3: FOC_DRV.Out_2, JFOC.pin3
  N4: FOC_DRV.Out_1, JFOC.pin2

custom parts:
  Raspberry Pi Pico: Raspberry Pi Pico. Based around the RP2040 microcontroller the Pico is a low cost microcontroller device bringing Raspberry Pi quality, cost, and easy of use to the microcontroller space. Jan 2021, Split part in to two versions: tht (this one) and SMD. This one will drill holes for a .1 in header in pcb to allow plugging in the module as well as providing pads to solder the module to the top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
  Generic male header - 2 pins: Generic male header
