# Fritzing sketch Heather-connection (saved by Fritzing 1.0.1rc)
circuit board: 8.46667cm x 5.64444cm
breadboards: 1

parts:
  PICO = Raspberry Pi Pico
  IC1 = IC, DIP package, 20 pins [chip_label=74HCT245P]
  R2 = Resistor [tolerance=±5% power=0.25 resistance=220k package=THT]
  Q1 = Basic FET N-Channel [package="TO220 [THT]"]
  J1 = female pin header, 5 pins [form="♀ (female)"]
  R3 = Resistor [tolerance=±5% power=0.25 resistance=4.7 package=THT]
  R4 = Resistor [tolerance=±5% power=0.25 resistance=220 package=THT]
  V3 = DC Power [voltage=12V]
  12V1 = Generic male header - 2 pins [form="♂ (male)" package=THT]

nets:
  GND: PICO.pin_3, PICO.pin_8, PICO.pin_13, PICO.pin_18, PICO.pin_23, PICO.pin_28, PICO.pin_33, PICO.pin_38, IC1.pin19, R2.Pin_1, Q1.source, J1.pin2, V3.V-, 12V1.GND
  Heat_temp_1: PICO.pin_17, J1.pin4, R3.Pin_0
  Heat_pw_1: PICO.pin_26, IC1.pin4
  3.3V: PICO.pin_36, J1.pin5, R3.Pin_1
  5V: PICO.pin_40, IC1.pin1, IC1.pin20
  N1: IC1.pin16, R4.Pin_0
  N2: R2.Pin_0, Q1.gate, R4.Pin_1
  N3: Q1.drain, J1.pin3
  12V: J1.pin1, V3.V+, 12V1.VIN

custom parts:
  Raspberry Pi Pico: Raspberry Pi Pico. Based around the RP2040 microcontroller the Pico is a low cost microcontroller device bringing Raspberry Pi quality, cost, and easy of use to the microcontroller space. Jan 2021, Split part in to two versions: tht (this one) and SMD. This one will drill holes for a .1 in header in pcb to allow plugging in the module as well as providing pads to solder the module to the top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
  Generic male header - 2 pins: Generic male header
