# Fritzing sketch Meteo (saved by Fritzing 1.0.1rc)
breadboards: 1

parts:
  PICO = Raspberry Pi Pico
  Composant1 = BME280 Breakout
  JMETEO = female pin header, 4 pins [form="♀ (female)"]

nets:
  GND/METEO_GND: PICO.pin_3, PICO.pin_8, PICO.pin_13, PICO.pin_18, PICO.pin_23, PICO.pin_28, PICO.pin_33, PICO.pin_38, Composant1.GND, JMETEO.pin1
  METEO_SCK: PICO.pin_21, Composant1.SCK/SCL, JMETEO.pin2
  METEO_SDI: PICO.pin_22, Composant1.SDI/SDA, JMETEO.pin3
  3.3V/METEO_VCC: PICO.pin_36, Composant1.3.3V, JMETEO.pin4

custom parts:
  Raspberry Pi Pico: Raspberry Pi Pico. Based around the RP2040 microcontroller the Pico is a low cost microcontroller device bringing Raspberry Pi quality, cost, and easy of use to the microcontroller space. Jan 2021, Split part in to two versions: tht (this one) and SMD. This one will drill holes for a .1 in header in pcb to allow plugging in the module as well as providing pads to solder the module to the top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
